# Fritzing sketch project (saved by Fritzing 1.0.4)
breadboards: 2

parts:
  Mod1 = Raspberry Pi Pico
  S1 = Pushbutton [package=THT]
  Display1 = LCD screen 16x2 HD44780
  R1 = Resistor [tolerance=±5% power=0.25W resistance=330 package=THT]
  R2 = Resistor [tolerance=±5% power=0.25W resistance=330 package=THT]

nets:
  N1: Mod1.pin_3, Mod1.pin_8, Mod1.pin_13, Mod1.pin_18, Mod1.pin_23, Mod1.pin_28, Mod1.pin_33, Mod1.pin_38, Display1.VSS, Display1.R_W, R2.Pin_0
  N2: Mod1.pin_5, S1.leg1
  N3: Mod1.pin_21, Display1.RS
  N4: Mod1.pin_22, Display1.E
  N5: Mod1.pin_24, Display1.DB4
  N6: Mod1.pin_25, Display1.DB5
  N7: Mod1.pin_26, Display1.DB6
  N8: Mod1.pin_27, Display1.DB7
  N9: Mod1.pin_36, S1.leg0
  N10: Mod1.pin_40, Display1.VDD, Display1.A
  N11: Display1.VO, R1.Pin_1
  N12: Display1.K, R2.Pin_1

custom parts:
  Raspberry Pi Pico: Raspberry Pi Pico. Based around the RP2040 microcontroller the Pico is a low cost microcontroller device bringing Raspberry Pi quality, cost, and easy of use to the microcontroller space. Jan 2021, Split part in to two versions: tht (this one) and SMD. This one will drill holes for a .1 in header in pcb to allow plugging in the module as well as providing pads to solder the module to the top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
  LCD screen 16x2 HD44780: LCD screen with HD44780 controller enables showing text, symbols, value or anything else that comes from Croduino/Arduino. It is capable of showing 16 symbols in two lines and therefore can be used in many projects that need to send clearly visible and legible output information.. • Color of symbols: White • Backlight: Blue • Dimensions: 80 x 36 x 12 mm • Screen dimensions: 64.5 x 16 mm •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
